// Logisim project 1BitAdder.circ as structural Verilog: 1 circuit, main circuit main
module main (
  input  A,
  input  B,
  input  Cin,
  output S,
  output Cout
);

  wire and_1_out, and_2_out, xor_1_out, xor_2_out;

  xor xor_1 (xor_1_out, A, B);
  and and_1 (and_1_out, A, B);
  and and_2 (and_2_out, Cin, xor_1_out);
  xor xor_2 (xor_2_out, A, B);
  or or_1 (Cout, and_1_out, and_2_out);
  xor xor_3 (S, xor_2_out, Cin);
endmodule
