// Logisim project 32BitAdder.circ as structural Verilog: 1 circuit, main circuit main
module main (
  input  [31:0] Multiplicand,
  input  [31:0] Product,
  output [31:0] sumOUT,
  output C32OUT
);

  wire _0_cout, _16_cout, main_1_cout, main_2_cout, main_3_cout, main_4_cout, main_5_cout, main_6_cout,
       main_7_cout, main_8_cout, main_9_cout, main_10_cout, main_11_cout, main_12_cout, main_13_cout,
       main_14_cout, main_15_cout, main_16_cout, main_17_cout, main_18_cout, main_19_cout, main_20_cout,
       main_21_cout, main_22_cout, main_23_cout, main_24_cout, main_25_cout, main_26_cout, main_27_cout,
       main_28_cout, main_29_cout;

  _1BitAdder_main _0 (.A(Multiplicand[0]), .B(Product[0]), .Cin(1'b0), .S(sumOUT[0]), .Cout(_0_cout));
  _1BitAdder_main main_1 (.A(Multiplicand[1]), .B(Product[1]), .Cin(_0_cout), .S(sumOUT[1]), .Cout(main_1_cout));
  _1BitAdder_main main_2 (.A(Multiplicand[2]), .B(Product[2]), .Cin(main_1_cout), .S(sumOUT[2]), .Cout(main_2_cout));
  _1BitAdder_main main_3 (.A(Multiplicand[3]), .B(Product[3]), .Cin(main_2_cout), .S(sumOUT[3]), .Cout(main_3_cout));
  _1BitAdder_main main_4 (.A(Multiplicand[4]), .B(Product[4]), .Cin(main_3_cout), .S(sumOUT[4]), .Cout(main_4_cout));
  _1BitAdder_main main_5 (.A(Multiplicand[5]), .B(Product[5]), .Cin(main_4_cout), .S(sumOUT[5]), .Cout(main_5_cout));
  _1BitAdder_main main_6 (.A(Multiplicand[6]), .B(Product[6]), .Cin(main_5_cout), .S(sumOUT[6]), .Cout(main_6_cout));
  _1BitAdder_main main_7 (.A(Multiplicand[7]), .B(Product[7]), .Cin(main_6_cout), .S(sumOUT[7]), .Cout(main_7_cout));
  _1BitAdder_main main_8 (.A(Multiplicand[8]), .B(Product[8]), .Cin(main_7_cout), .S(sumOUT[8]), .Cout(main_8_cout));
  _1BitAdder_main main_9 (.A(Multiplicand[9]), .B(Product[9]), .Cin(main_8_cout), .S(sumOUT[9]), .Cout(main_9_cout));
  _1BitAdder_main main_10 (
    .A(Multiplicand[10]), .B(Product[10]), .Cin(main_9_cout), .S(sumOUT[10]), .Cout(main_10_cout));
  _1BitAdder_main main_11 (
    .A(Multiplicand[11]), .B(Product[11]), .Cin(main_10_cout), .S(sumOUT[11]), .Cout(main_11_cout));
  _1BitAdder_main main_12 (
    .A(Multiplicand[12]), .B(Product[12]), .Cin(main_11_cout), .S(sumOUT[12]), .Cout(main_12_cout));
  _1BitAdder_main main_13 (
    .A(Multiplicand[13]), .B(Product[13]), .Cin(main_12_cout), .S(sumOUT[13]), .Cout(main_13_cout));
  _1BitAdder_main main_14 (
    .A(Multiplicand[14]), .B(Product[14]), .Cin(main_13_cout), .S(sumOUT[14]), .Cout(main_14_cout));
  _1BitAdder_main main_15 (
    .A(Multiplicand[15]), .B(Product[15]), .Cin(main_14_cout), .S(sumOUT[15]), .Cout(main_15_cout));
  _1BitAdder_main _16 (.A(Multiplicand[16]), .B(Product[16]), .Cin(main_15_cout), .S(sumOUT[16]), .Cout(_16_cout));
  _1BitAdder_main main_16 (.A(Multiplicand[17]), .B(Product[17]), .Cin(_16_cout), .S(sumOUT[17]), .Cout(main_16_cout));
  _1BitAdder_main main_17 (
    .A(Multiplicand[18]), .B(Product[18]), .Cin(main_16_cout), .S(sumOUT[18]), .Cout(main_17_cout));
  _1BitAdder_main main_18 (
    .A(Multiplicand[19]), .B(Product[19]), .Cin(main_17_cout), .S(sumOUT[19]), .Cout(main_18_cout));
  _1BitAdder_main main_19 (
    .A(Multiplicand[20]), .B(Product[20]), .Cin(main_18_cout), .S(sumOUT[20]), .Cout(main_19_cout));
  _1BitAdder_main main_20 (
    .A(Multiplicand[21]), .B(Product[21]), .Cin(main_19_cout), .S(sumOUT[21]), .Cout(main_20_cout));
  _1BitAdder_main main_21 (
    .A(Multiplicand[22]), .B(Product[22]), .Cin(main_20_cout), .S(sumOUT[22]), .Cout(main_21_cout));
  _1BitAdder_main main_22 (
    .A(Multiplicand[23]), .B(Product[23]), .Cin(main_21_cout), .S(sumOUT[23]), .Cout(main_22_cout));
  _1BitAdder_main main_23 (
    .A(Multiplicand[24]), .B(Product[24]), .Cin(main_22_cout), .S(sumOUT[24]), .Cout(main_23_cout));
  _1BitAdder_main main_24 (
    .A(Multiplicand[25]), .B(Product[25]), .Cin(main_23_cout), .S(sumOUT[25]), .Cout(main_24_cout));
  _1BitAdder_main main_25 (
    .A(Multiplicand[26]), .B(Product[26]), .Cin(main_24_cout), .S(sumOUT[26]), .Cout(main_25_cout));
  _1BitAdder_main main_26 (
    .A(Multiplicand[27]), .B(Product[27]), .Cin(main_25_cout), .S(sumOUT[27]), .Cout(main_26_cout));
  _1BitAdder_main main_27 (
    .A(Multiplicand[28]), .B(Product[28]), .Cin(main_26_cout), .S(sumOUT[28]), .Cout(main_27_cout));
  _1BitAdder_main main_28 (
    .A(Multiplicand[29]), .B(Product[29]), .Cin(main_27_cout), .S(sumOUT[29]), .Cout(main_28_cout));
  _1BitAdder_main main_29 (
    .A(Multiplicand[30]), .B(Product[30]), .Cin(main_28_cout), .S(sumOUT[30]), .Cout(main_29_cout));
  _1BitAdder_main main_30 (.A(Multiplicand[31]), .B(Product[31]), .Cin(main_29_cout), .S(sumOUT[31]), .Cout(C32OUT));
endmodule
