// Logisim project 64BitShifter.circ as structural Verilog: 1 circuit, main circuit main
module main (
  input  [31:0] LEFT32,
  input  Cout,
  input  [31:0] RIGHT32,
  output [31:0] LEFT32OUT,
  output [31:0] RIGHT32OUT
);


  assign LEFT32OUT = {Cout, LEFT32[31:1]};
  assign RIGHT32OUT = {LEFT32[0], RIGHT32[31:1]};
endmodule
