// Logisim project control.circ as structural Verilog: 1 circuit, main circuit ControlUnit
module ControlUnit (
  input  go,
  input  lsb,
  input  ctr_32,
  input  clk,
  output _0toProduct,
  output loadCtr,
  output MULTPLR,
  output \SHİFTtOREG ,
  output CNT,
  output SaveProdL,
  output SaveProdR
);

  wire and_1_out, and_2_out, and_3_out, and_4_out, and_5_out, and_6_out, and_8_out, and_9_out, not_1_out,
       not_2_out, not_3_out, not_4_out, not_5_out, not_6_out, not_7_out, not_8_out, not_9_out, not_10_out,
       not_11_out, not_12_out, not_13_out, not_14_out, not_15_out, not_16_out, or_1_out, or_2_out, or_3_out,
       xor_1_out;
  wire [2:0] n0_out, register_1_q;

  Register #(.width(3)) register_1 (.D(n0_out), .Q(register_1_q), .clk(clk));  // open: en, clr
  not not_1 (not_1_out, lsb);
  not not_2 (not_2_out, ctr_32);
  not not_3 (not_3_out, register_1_q[0]);
  or or_1 (or_1_out, register_1_q[0], not_1_out);
  or or_2 (or_2_out, not_2_out, not_3_out);
  not not_4 (not_4_out, register_1_q[2]);
  not not_5 (not_5_out, register_1_q[1]);
  not not_6 (not_6_out, register_1_q[1]);
  not not_7 (not_7_out, register_1_q[0]);
  not not_8 (not_8_out, register_1_q[2]);
  or or_3 (or_3_out, register_1_q[2], go);
  and and_1 (and_1_out, not_4_out, register_1_q[1], or_1_out);
  and and_2 (and_2_out, register_1_q[2], not_5_out, or_2_out);
  and and_3 (and_3_out, not_6_out, register_1_q[0]);
  and and_4 (and_4_out, register_1_q[1], not_7_out, not_8_out, lsb);
  not not_9 (not_9_out, register_1_q[0]);
  not not_10 (not_10_out, register_1_q[1]);
  not not_11 (not_11_out, register_1_q[2]);
  or n2 (n0_out[2], and_1_out, and_2_out);
  or n1 (n0_out[1], and_3_out, and_4_out);
  and and_5 (and_5_out, not_9_out, not_10_out, or_3_out);
  and and_6 (and_6_out, not_11_out, register_1_q[1], not_9_out, lsb);
  or n0 (n0_out[0], and_5_out, and_6_out);
  not not_12 (not_12_out, register_1_q[2]);
  not not_13 (not_13_out, register_1_q[1]);
  not not_14 (not_14_out, register_1_q[2]);
  not not_15 (not_15_out, register_1_q[0]);
  and and_7 (_0toProduct, not_12_out, not_13_out, register_1_q[0]);
  and and_8 (and_8_out, not_14_out, register_1_q[0]);
  and and_9 (and_9_out, register_1_q[2], not_13_out, not_15_out);
  not not_16 (not_16_out, register_1_q[0]);
  and and_10 (CNT, register_1_q[2], not_13_out, not_16_out);
  or PL (SaveProdL, and_8_out, and_9_out);
  xor xor_1 (xor_1_out, register_1_q[2], register_1_q[0]);
  and and_11 (SaveProdR, xor_1_out, not_13_out);

  assign loadCtr = _0toProduct;
  assign MULTPLR = _0toProduct;
  assign \SHİFTtOREG  = CNT;

  // Notes on the sheet:
  //   s2
  //   s0
  //   n0
  //   n2
endmodule
