// Logisim project datapath.circ as structural Verilog: 4 circuits, main circuit DataPath
module DataPath (
  input  [31:0] MULTIPLICANT,
  input  _0toProduct,
  input  ShiftToReg,
  input  SaveProductleft,
  input  SaveProductRight,
  input  MLTPLR,
  input  [31:0] MULTIPLIER,
  input  CLK,
  input  LoadCtr,
  input  CNT,
  output [31:0] \OUTFİRST32 ,
  output [31:0] OUTSECOND32,
  output LSB,
  output ctr_32
);

  wire carryRegister_q, n32bitadder_1_c32out, not_1_out;
  wire [6:0] counter_1_q;
  wire [31:0] multiplexer_1_out, multiplexer_2_out, multiplexer_3_out, multiplexer_4_out,
       n32bitadder_1_sumout, n64bitshifter_1_left32out, n64bitshifter_1_right32out;

  not not_1 (not_1_out, ShiftToReg);
  _32BitAdder u_32bitadder_1 (
    .Multiplicand(\OUTFİRST32 ), .Product(MULTIPLICANT), .sumOUT(n32bitadder_1_sumout),
    .C32OUT(n32bitadder_1_c32out));
  Register #(.width(1)) carryRegister (
    .D(n32bitadder_1_c32out), .en(not_1_out), .Q(carryRegister_q));  // open: clk, clr
  Multiplexer #(.width(32), .enable("false")) multiplexer_1 (
    .in0(n32bitadder_1_sumout), .in1({32{1'b0}}), .out(multiplexer_1_out), .sel(_0toProduct));
  Multiplexer #(.width(32), .enable("false")) multiplexer_2 (
    .in0({OUTSECOND32[31:1], LSB}), .in1(MULTIPLIER), .out(multiplexer_2_out), .sel(MLTPLR));
  Counter #(.width(7), .max('h7f)) counter_1 (
    .load(LoadCtr), .count(CNT), .Q(counter_1_q), .clk(CLK));  // open: D, carry, clr
  Multiplexer #(.width(32), .enable("false")) multiplexer_3 (
    .in0(multiplexer_1_out), .in1(n64bitshifter_1_left32out), .out(multiplexer_3_out), .sel(ShiftToReg));
  Multiplexer #(.width(32), .enable("false")) multiplexer_4 (
    .in0(multiplexer_2_out), .in1(n64bitshifter_1_right32out), .out(multiplexer_4_out), .sel(ShiftToReg));
  Register #(.width(32)) registerLeft (
    .D(multiplexer_3_out), .en(SaveProductleft), .Q(\OUTFİRST32 ), .clk(CLK));  // open: clr
  Register #(.width(32)) registerRight (
    .D(multiplexer_4_out), .en(SaveProductRight), .Q({OUTSECOND32[31:1], LSB}), .clk(CLK));  // open: clr
  _64BitShifter u_64bitshifter_1 (
    .LEFT32(\OUTFİRST32 ), .Cout(carryRegister_q), .RIGHT32({OUTSECOND32[31:1], LSB}),
    .LEFT32OUT(n64bitshifter_1_left32out), .RIGHT32OUT(n64bitshifter_1_right32out));
  Comparator #(.width(7), .mode("unsigned")) comparator_1 (
    .a(counter_1_q), .b(7'b0100000), .lt(ctr_32));  // open: gt, eq

  assign OUTSECOND32[0] = LSB;
endmodule

module _1BitAdder (
  input  A,
  input  B,
  input  Cin,
  output S,
  output Cout
);

  wire and_1_out, and_2_out, xor_1_out, xor_2_out;

  xor xor_1 (xor_1_out, A, B);
  and and_1 (and_1_out, A, B);
  and and_2 (and_2_out, Cin, xor_1_out);
  xor xor_2 (xor_2_out, A, B);
  or or_1 (Cout, and_1_out, and_2_out);
  xor xor_3 (S, xor_2_out, Cin);
endmodule

module _32BitAdder (
  input  [31:0] Multiplicand,
  input  [31:0] Product,
  output [31:0] sumOUT,
  output C32OUT
);

  wire n1bitadder_1_cout, n1bitadder_2_cout, n1bitadder_3_cout, n1bitadder_4_cout, n1bitadder_5_cout,
       n1bitadder_6_cout, n1bitadder_7_cout, n1bitadder_8_cout, n1bitadder_9_cout, n1bitadder_10_cout,
       n1bitadder_11_cout, n1bitadder_12_cout, n1bitadder_13_cout, n1bitadder_14_cout, n1bitadder_15_cout,
       n1bitadder_16_cout, n1bitadder_17_cout, n1bitadder_18_cout, n1bitadder_19_cout, n1bitadder_20_cout,
       n1bitadder_21_cout, n1bitadder_22_cout, n1bitadder_23_cout, n1bitadder_24_cout, n1bitadder_25_cout,
       n1bitadder_26_cout, n1bitadder_27_cout, n1bitadder_28_cout, n1bitadder_29_cout, n1bitadder_30_cout,
       n1bitadder_31_cout;

  _1BitAdder u_1bitadder_1 (.A(Multiplicand[0]), .B(Product[0]), .Cin(1'b0), .S(sumOUT[0]), .Cout(n1bitadder_1_cout));
  _1BitAdder u_1bitadder_2 (
    .A(Multiplicand[1]), .B(Product[1]), .Cin(n1bitadder_1_cout), .S(sumOUT[1]), .Cout(n1bitadder_2_cout));
  _1BitAdder u_1bitadder_3 (
    .A(Multiplicand[2]), .B(Product[2]), .Cin(n1bitadder_2_cout), .S(sumOUT[2]), .Cout(n1bitadder_3_cout));
  _1BitAdder u_1bitadder_4 (
    .A(Multiplicand[3]), .B(Product[3]), .Cin(n1bitadder_3_cout), .S(sumOUT[3]), .Cout(n1bitadder_4_cout));
  _1BitAdder u_1bitadder_5 (
    .A(Multiplicand[4]), .B(Product[4]), .Cin(n1bitadder_4_cout), .S(sumOUT[4]), .Cout(n1bitadder_5_cout));
  _1BitAdder u_1bitadder_6 (
    .A(Multiplicand[5]), .B(Product[5]), .Cin(n1bitadder_5_cout), .S(sumOUT[5]), .Cout(n1bitadder_6_cout));
  _1BitAdder u_1bitadder_7 (
    .A(Multiplicand[6]), .B(Product[6]), .Cin(n1bitadder_6_cout), .S(sumOUT[6]), .Cout(n1bitadder_7_cout));
  _1BitAdder u_1bitadder_8 (
    .A(Multiplicand[7]), .B(Product[7]), .Cin(n1bitadder_7_cout), .S(sumOUT[7]), .Cout(n1bitadder_8_cout));
  _1BitAdder u_1bitadder_9 (
    .A(Multiplicand[8]), .B(Product[8]), .Cin(n1bitadder_8_cout), .S(sumOUT[8]), .Cout(n1bitadder_9_cout));
  _1BitAdder u_1bitadder_10 (
    .A(Multiplicand[9]), .B(Product[9]), .Cin(n1bitadder_9_cout), .S(sumOUT[9]), .Cout(n1bitadder_10_cout));
  _1BitAdder u_1bitadder_11 (
    .A(Multiplicand[10]), .B(Product[10]), .Cin(n1bitadder_10_cout), .S(sumOUT[10]), .Cout(n1bitadder_11_cout));
  _1BitAdder u_1bitadder_12 (
    .A(Multiplicand[11]), .B(Product[11]), .Cin(n1bitadder_11_cout), .S(sumOUT[11]), .Cout(n1bitadder_12_cout));
  _1BitAdder u_1bitadder_13 (
    .A(Multiplicand[12]), .B(Product[12]), .Cin(n1bitadder_12_cout), .S(sumOUT[12]), .Cout(n1bitadder_13_cout));
  _1BitAdder u_1bitadder_14 (
    .A(Multiplicand[13]), .B(Product[13]), .Cin(n1bitadder_13_cout), .S(sumOUT[13]), .Cout(n1bitadder_14_cout));
  _1BitAdder u_1bitadder_15 (
    .A(Multiplicand[14]), .B(Product[14]), .Cin(n1bitadder_14_cout), .S(sumOUT[14]), .Cout(n1bitadder_15_cout));
  _1BitAdder u_1bitadder_16 (
    .A(Multiplicand[15]), .B(Product[15]), .Cin(n1bitadder_15_cout), .S(sumOUT[15]), .Cout(n1bitadder_16_cout));
  _1BitAdder u_1bitadder_17 (
    .A(Multiplicand[16]), .B(Product[16]), .Cin(n1bitadder_16_cout), .S(sumOUT[16]), .Cout(n1bitadder_17_cout));
  _1BitAdder u_1bitadder_18 (
    .A(Multiplicand[17]), .B(Product[17]), .Cin(n1bitadder_17_cout), .S(sumOUT[17]), .Cout(n1bitadder_18_cout));
  _1BitAdder u_1bitadder_19 (
    .A(Multiplicand[18]), .B(Product[18]), .Cin(n1bitadder_18_cout), .S(sumOUT[18]), .Cout(n1bitadder_19_cout));
  _1BitAdder u_1bitadder_20 (
    .A(Multiplicand[19]), .B(Product[19]), .Cin(n1bitadder_19_cout), .S(sumOUT[19]), .Cout(n1bitadder_20_cout));
  _1BitAdder u_1bitadder_21 (
    .A(Multiplicand[20]), .B(Product[20]), .Cin(n1bitadder_20_cout), .S(sumOUT[20]), .Cout(n1bitadder_21_cout));
  _1BitAdder u_1bitadder_22 (
    .A(Multiplicand[21]), .B(Product[21]), .Cin(n1bitadder_21_cout), .S(sumOUT[21]), .Cout(n1bitadder_22_cout));
  _1BitAdder u_1bitadder_23 (
    .A(Multiplicand[22]), .B(Product[22]), .Cin(n1bitadder_22_cout), .S(sumOUT[22]), .Cout(n1bitadder_23_cout));
  _1BitAdder u_1bitadder_24 (
    .A(Multiplicand[23]), .B(Product[23]), .Cin(n1bitadder_23_cout), .S(sumOUT[23]), .Cout(n1bitadder_24_cout));
  _1BitAdder u_1bitadder_25 (
    .A(Multiplicand[24]), .B(Product[24]), .Cin(n1bitadder_24_cout), .S(sumOUT[24]), .Cout(n1bitadder_25_cout));
  _1BitAdder u_1bitadder_26 (
    .A(Multiplicand[25]), .B(Product[25]), .Cin(n1bitadder_25_cout), .S(sumOUT[25]), .Cout(n1bitadder_26_cout));
  _1BitAdder u_1bitadder_27 (
    .A(Multiplicand[26]), .B(Product[26]), .Cin(n1bitadder_26_cout), .S(sumOUT[26]), .Cout(n1bitadder_27_cout));
  _1BitAdder u_1bitadder_28 (
    .A(Multiplicand[27]), .B(Product[27]), .Cin(n1bitadder_27_cout), .S(sumOUT[27]), .Cout(n1bitadder_28_cout));
  _1BitAdder u_1bitadder_29 (
    .A(Multiplicand[28]), .B(Product[28]), .Cin(n1bitadder_28_cout), .S(sumOUT[28]), .Cout(n1bitadder_29_cout));
  _1BitAdder u_1bitadder_30 (
    .A(Multiplicand[29]), .B(Product[29]), .Cin(n1bitadder_29_cout), .S(sumOUT[29]), .Cout(n1bitadder_30_cout));
  _1BitAdder u_1bitadder_31 (
    .A(Multiplicand[30]), .B(Product[30]), .Cin(n1bitadder_30_cout), .S(sumOUT[30]), .Cout(n1bitadder_31_cout));
  _1BitAdder u_1bitadder_32 (
    .A(Multiplicand[31]), .B(Product[31]), .Cin(n1bitadder_31_cout), .S(sumOUT[31]), .Cout(C32OUT));
endmodule

module _64BitShifter (
  input  [31:0] LEFT32,
  input  Cout,
  input  [31:0] RIGHT32,
  output [31:0] LEFT32OUT,
  output [31:0] RIGHT32OUT
);


  assign LEFT32OUT = {Cout, LEFT32[31:1]};
  assign RIGHT32OUT = {LEFT32[0], RIGHT32[31:1]};
endmodule
