// Logisim project mult32.circ as structural Verilog: 1 circuit, main circuit mult32
module mult32 (
  input  [31:0] Multiplicant,
  input  [31:0] Multiplier,
  output [31:0] FirstOut,
  output [31:0] SecondOut
);

  wire clock_1_out, controlunit_1__0toproduct, controlunit_1_cnt, controlunit_1_loadctr,
       controlunit_1_multplr, controlunit_1_saveprodl, controlunit_1_saveprodr, \controlunit_1_shi̇fttoreg ,
       datapath_1_ctr_32, datapath_1_lsb, go_out;

  Clock clock_1 (.out(clock_1_out));
  Button go (.out(go_out));
  DataPath datapath_1 (
    .MULTIPLICANT(Multiplicant), ._0toProduct(controlunit_1__0toproduct),
    .ShiftToReg(\controlunit_1_shi̇fttoreg ), .SaveProductleft(controlunit_1_saveprodl),
    .SaveProductRight(controlunit_1_saveprodr), .MLTPLR(controlunit_1_multplr), .MULTIPLIER(Multiplier),
    .CLK(clock_1_out), .LoadCtr(controlunit_1_loadctr), .CNT(controlunit_1_cnt), .\OUTFİRST32 (FirstOut),
    .OUTSECOND32(SecondOut), .LSB(datapath_1_lsb), .ctr_32(datapath_1_ctr_32));
  ControlUnit controlunit_1 (
    .go(go_out), .lsb(datapath_1_lsb), .ctr_32(datapath_1_ctr_32), .clk(clock_1_out),
    ._0toProduct(controlunit_1__0toproduct), .loadCtr(controlunit_1_loadctr),
    .MULTPLR(controlunit_1_multplr), .\SHİFTtOREG (\controlunit_1_shi̇fttoreg ), .CNT(controlunit_1_cnt),
    .SaveProdL(controlunit_1_saveprodl), .SaveProdR(controlunit_1_saveprodr));
endmodule
